// Digital circuit 4 bit adder digital.dig as structural Verilog
module _4_bit_adder_digital (
  input  in_1,
  input  in_2,
  input  in_3,
  input  in_4,
  input  in_5,
  input  in_6,
  input  in_7,
  input  in_8,
  input  in_14,
  output out_9,
  output out_10,
  output out_11,
  output out_12,
  output out_13
);

  wire add_2_c_o, add_3_c_o, add_4_c_o, xor_1_out, xor_2_out, xor_3_out, xor_4_out;

  xor xor_1 (xor_1_out, in_14, in_1);
  Add add_1 (.a(in_2), .b(xor_1_out), .c_i(add_2_c_o), .s(out_12), .c_o(out_13));
  xor xor_2 (xor_2_out, in_14, in_3);
  Add add_2 (.a(in_4), .b(xor_2_out), .c_i(add_3_c_o), .s(out_11), .c_o(add_2_c_o));
  xor xor_3 (xor_3_out, in_14, in_5);
  Add add_3 (.a(in_6), .b(xor_3_out), .c_i(add_4_c_o), .s(out_10), .c_o(add_3_c_o));
  xor xor_4 (xor_4_out, in_14, in_7);
  Add add_4 (.a(in_8), .b(xor_4_out), .c_i(in_14), .s(out_9), .c_o(add_4_c_o));
endmodule
