// Digital circuit 8 BIT ADDER WITH SUB.dig as structural Verilog
module _8_BIT_ADDER_WITH_SUB (
  input  B7,
  input  B6,
  input  B5,
  input  B4,
  input  B3,
  input  B2,
  input  B1,
  input  B0,
  input  INVERT,
  input  A0,
  input  A1,
  input  A2,
  input  A3,
  input  A4,
  input  A5,
  input  A6,
  input  A7,
  output out_18,
  output out_19,
  output out_20,
  output out_21,
  output out_22,
  output out_23,
  output out_24,
  output out_25,
  output out_26
);

  wire add_1_c_o, add_2_c_o, add_3_c_o, add_4_c_o, add_5_c_o, add_6_c_o, add_7_c_o, add_8_c_o, not_1_out,
       xor_2_out, xor_3_out, xor_4_out, xor_5_out, xor_6_out, xor_7_out, xor_8_out, xor_9_out;

  not not_1 (not_1_out, INVERT);
  xor xor_1 (out_26, add_1_c_o, INVERT);
  Add add_1 (.a(A7), .b(xor_2_out), .c_i(add_2_c_o), .s(out_18), .c_o(add_1_c_o));
  xor xor_2 (xor_2_out, B7, not_1_out);
  Add add_2 (.a(A6), .b(xor_3_out), .c_i(add_3_c_o), .s(out_19), .c_o(add_2_c_o));
  xor xor_3 (xor_3_out, B6, not_1_out);
  Add add_3 (.a(A5), .b(xor_4_out), .c_i(add_4_c_o), .s(out_20), .c_o(add_3_c_o));
  xor xor_4 (xor_4_out, B5, not_1_out);
  Add add_4 (.a(A4), .b(xor_5_out), .c_i(add_5_c_o), .s(out_21), .c_o(add_4_c_o));
  xor xor_5 (xor_5_out, B4, not_1_out);
  Add add_5 (.a(A3), .b(xor_6_out), .c_i(add_6_c_o), .s(out_22), .c_o(add_5_c_o));
  xor xor_6 (xor_6_out, B3, not_1_out);
  Add add_6 (.a(A2), .b(xor_7_out), .c_i(add_7_c_o), .s(out_23), .c_o(add_6_c_o));
  xor xor_7 (xor_7_out, B2, not_1_out);
  Add add_7 (.a(A1), .b(xor_8_out), .c_i(add_8_c_o), .s(out_24), .c_o(add_7_c_o));
  xor xor_8 (xor_8_out, B1, not_1_out);
  Add add_8 (.a(A0), .b(xor_9_out), .c_i(INVERT), .s(out_25), .c_o(add_8_c_o));
  xor xor_9 (xor_9_out, B0, not_1_out);

  // Notes on the sheet:
  //   8 Bit Adder With Sub
endmodule
