// Digital circuit 8 bit adder (I think).dig as structural Verilog
module _8_bit_adder__I_think (
  input  in_1,
  input  in_2,
  input  in_3,
  input  in_4,
  input  in_7,
  input  in_8,
  input  in_9,
  input  in_10,
  input  in_13,
  input  in_14,
  input  in_15,
  input  in_16,
  input  in_19,
  input  in_20,
  input  in_21,
  input  in_22,
  input  in_26,
  output out_5,
  output out_6,
  output out_11,
  output out_12,
  output out_17,
  output out_18,
  output out_23,
  output out_24,
  output out_25
);

  wire add_2_c_o, add_3_c_o, add_4_c_o, add_5_c_o, add_6_c_o, add_7_c_o, add_8_c_o;

  Add add_1 (.a(in_19), .b(in_21), .c_i(add_2_c_o), .s(out_24), .c_o(out_25));
  Add add_2 (.a(in_20), .b(in_22), .c_i(add_3_c_o), .s(out_23), .c_o(add_2_c_o));
  Add add_3 (.a(in_13), .b(in_15), .c_i(add_4_c_o), .s(out_18), .c_o(add_3_c_o));
  Add add_4 (.a(in_14), .b(in_16), .c_i(add_5_c_o), .s(out_17), .c_o(add_4_c_o));
  Add add_5 (.a(in_7), .b(in_9), .c_i(add_6_c_o), .s(out_12), .c_o(add_5_c_o));
  Add add_6 (.a(in_8), .b(in_10), .c_i(add_7_c_o), .s(out_11), .c_o(add_6_c_o));
  Add add_7 (.a(in_1), .b(in_3), .c_i(add_8_c_o), .s(out_6), .c_o(add_7_c_o));
  Add add_8 (.a(in_2), .b(in_4), .c_i(in_26), .s(out_5), .c_o(add_8_c_o));

  // Notes on the sheet:
  //   8 Bit Adder
endmodule
