// Digital circuit FLIP FLOP.dig as structural Verilog
module FLIP_FLOP (
  input  in_1,
  input  in_2
);

  wire nor_1_out, nor_2_out;

  nor nor_1 (nor_1_out, nor_2_out, in_1);
  nor nor_2 (nor_2_out, nor_1_out, in_2);
  LED led_1 (.in(nor_2_out));

  // Notes on the sheet:
  //   D flip flop
endmodule
