// Digital circuit Half Adder Digital.dig as structural Verilog
module Half_Adder_Digital (
  input  A,
  input  B,
  input  A_2,
  input  B_2,
  input  Cin,
  output S,
  output Cout,
  output S_2,
  output Cout_2
);

  wire and_2_out, and_3_out, xor_2_out;

  xor xor_1 (S, A, B);
  and and_1 (Cout, A, B);
  xor xor_2 (xor_2_out, A_2, B_2);
  and and_2 (and_2_out, A_2, B_2);
  xor xor_3 (S_2, xor_2_out, Cin);
  and and_3 (and_3_out, Cin, xor_2_out);
  or or_1 (Cout_2, and_2_out, and_3_out);

  // Notes on the sheet:
  //   Half Adder
  //   Full Adder
endmodule
