// Logisim project Half Adder.circ as structural Verilog: 1 circuit, main circuit half adder
module half_adder (
);

  wire and_1_out, button_1_out, button_2_out, xor_1_out;

  Button button_1 (.out(button_1_out));
  Button button_2 (.out(button_2_out));
  and and_1 (and_1_out, button_1_out, button_2_out);
  LED led_1 (.in(xor_1_out));
  xor xor_1 (xor_1_out, button_1_out, button_2_out);
  LED led_2 (.in(and_1_out));
endmodule
