// Digital circuit ripple counter.dig as structural Verilog
module ripple_counter (
  input  clk,
  input  in_2,
  output out_3,
  output out_4
);

  wire jk_ff_1_nq, jk_ff_2_nq;

  JK_FF jk_ff_1 (.J(in_2), .C(clk), .K(in_2), .nQ(jk_ff_1_nq));  // open: Q
  JK_FF jk_ff_2 (.J(in_2), .C(jk_ff_1_nq), .K(in_2), .nQ(jk_ff_2_nq));  // open: Q
  JK_FF jk_ff_3 (.J(in_2), .C(jk_ff_2_nq), .K(in_2), .Q(out_3), .nQ(out_4));

  // Notes on the sheet:
  //   Ripple Counter
endmodule
